# Fritzing sketch TFT (saved by Fritzing 0.9.3b)
breadboards: 1

parts:
  Arduino = Arduino Uno (Rev3) - ICSP
  PS2_Joystick = Thumb Joystick
  R1 = Resistor [tolerance=±5% resistance=470 package=THT]
  Part1 = ws2812b [package="smd 2812b"]
  R2 = Resistor [tolerance=±5% resistance=1k package=THT]
  SD_Card_reader = MicroSD Card Module

nets:
  N1: Arduino.A0, PS2_Joystick.HORZ
  N2: Arduino.A1, PS2_Joystick.VERT
  N3: Arduino.D11_PWM/MOSI, SD_Card_reader.MOSI
  N4: Arduino.D12/MISO, SD_Card_reader.MISO
  N5: Arduino.D13/SCK, SD_Card_reader.SCK
  GND: Arduino.GND, PS2_Joystick.GND, Part1.VSS, SD_Card_reader.GND
  VCC: Arduino.D3_PWM, Arduino.VIN, PS2_Joystick.SEL, PS2_Joystick.VCC, Part1.VDD, R2.Pin_0, R2.Pin_1, SD_Card_reader.VCC
  N6: Arduino.D4, SD_Card_reader.CS
  N7: Arduino.D6_PWM, R1.Pin_1
  N8: R1.Pin_0, Part1.DIN
